# Fritzing sketch Schemat (saved by Fritzing 0.9.4)

parts:
  R1 = Resistor [tolerance=±5% resistance=4.7k package=THT]
  Arduino = Arduino Nano (Rev3.0)
  DS18B20_1 = TEMPERATURE-SENSOR [package=to-92]
  DS18B20_2 = TEMPERATURE-SENSOR [package=to-92]
  DS18B20_3_itd = TEMPERATURE-SENSOR [package=to-92]
  J1 = Peltier Element
  9-16V = BANANA_CONN [package=banana_conn]
  GND = BANANA_CONN [package=banana_conn]
  Czujnik_temp_otoczenia = TEMPERATURE-SENSOR [package=to-92]

nets:
  N1: R1.Pin_0, Arduino.D10, DS18B20_1.ADJ, DS18B20_2.ADJ, DS18B20_3_itd.ADJ
  VCC: R1.Pin_1, Arduino.5V, DS18B20_1.VCC, DS18B20_2.VCC, DS18B20_3_itd.VCC, Czujnik_temp_otoczenia.VCC
  GND: Arduino.GND, DS18B20_1.GND, DS18B20_2.GND, DS18B20_3_itd.GND, Czujnik_temp_otoczenia.GND
  N2: Arduino.A0, Czujnik_temp_otoczenia.ADJ
  N3: J1.pin1, GND.1
  N4: J1.pin2, 9-16V.1
